# Fritzing sketch ClockStream (saved by Fritzing 0.9.3b)
circuit board: 8.46667cm x 5.64444cm
perfboards: 1

parts:
  Part1 = Arduino Nano (Rev3.0)
  IC1 = SHIFT REGISTER [package=dil16]
  ZS-042_RTC1 = ZS-042 RTC Module
  R1 = Photocell (LDR) [package=THT]  # not connected
  JP1 = Header 12 [package=1x12_machine-pin-header_lock.004]  # not connected
  RHT1 = Humidity and Temperature Sensor RHT03

nets:
  N1: Part1.GND, RHT1.GND_1
  N2: Part1.5V, IC1.SCL
  N3: Part1.A5, ZS-042_RTC1.SCL
  N4: Part1.A4, ZS-042_RTC1.SDA

notes:
  D11 - White to 7 Seg
  DHT11 - -ve, -ve, data, +ve
  D3 - Gray - Switch
  A0 - Yellow to 7 Seg
  A1 - Green to 7 Seg
  A2 - Orange to 7 Seg
  A3 - White to 7 Seg
  Green to 7 Seg
  Yellow to 7 Seg
  Green to 7 Seg
  Yellow to 7 Seg
  Yellow to 7 Seg
  Purple to 7 Seg
