# Fritzing sketch ClockStreamToBe (saved by Fritzing 0.9.3b)
circuit board: 8.46667cm x 5.64444cm
perfboards: 3

parts:
  Part1 = Arduino Nano (Rev3.0)
  IC1 = SHIFT REGISTER [package=dil16]
  ZS-042_RTC1 = ZS-042 RTC Module
  RHT1 = Humidity and Temperature Sensor RHT03
  IC2 = SHIFT REGISTER [package=dil16]
  R1 = Resistor [tolerance=±5% resistance=220 package=THT]  # not connected
  R2 = Resistor [tolerance=±5% resistance=220 package=THT]  # not connected
  R3 = Resistor [tolerance=±5% resistance=220 package=THT]  # not connected
  R4 = Resistor [tolerance=±5% resistance=220 package=THT]  # not connected
  R5 = Resistor [tolerance=±5% resistance=220 package=THT]  # not connected
  R6 = Resistor [tolerance=±5% resistance=220 package=THT]  # not connected
  R7 = Resistor [tolerance=±5% resistance=220 package=THT]  # not connected
  R8 = Resistor [tolerance=±5% resistance=220 package=THT]  # not connected
  Part2 = Arduino Nano (Rev3.0)
  IC3 = SHIFT REGISTER [package=dil16]
  ZS-042_RTC2 = ZS-042 RTC Module
  RHT2 = Humidity and Temperature Sensor RHT03

nets:
  N1: Part1.GND, RHT1.GND_1
  N2: Part1.D5, RHT1.Vcc
  N3: Part1.D6, IC1.SER
  N4: Part1.D7, IC1.SCK
  N5: Part1.D9, RHT1.Data-signal
  N6: Part1.5V, IC1.SCL
  N7: Part1.A5, ZS-042_RTC1.SCL
  N8: Part1.A4, ZS-042_RTC1.SDA
  N9: IC2.QH*, IC2.VCC
  GND: Part2.GND, ZS-042_RTC2.GND
  N10: Part2.D4, IC3.VCC
  N11: Part2.D5, RHT2.Vcc
  N12: Part2.D6, IC3.SER
  N13: Part2.D7, IC3.RCK
  N14: Part2.D8, IC3.SCK
  N15: Part2.D9, RHT2.Data-signal
  N16: Part2.5V, IC3.SCL
  N17: Part2.A5, ZS-042_RTC2.SCL
  N18: Part2.A4, ZS-042_RTC2.SDA
  N19: IC3.GND, IC3.G

notes:
  D11 - White to 7 Seg
  DHT11 - -ve, -ve, data, +ve
  D3 - Gray - Switch
  A0 - Yellow to 7 Seg
  A1 - Green to 7 Seg
  A2 - Orange to 7 Seg
  A3 - White to 7 Seg
  Green to 7 Seg
  Yellow to 7 Seg
  Green to 7 Seg
  Yellow to 7 Seg
  Yellow to 7 Seg
  Purple to 7 Seg
